# Fritzing sketch Circuit (saved by Fritzing 0.9.9b)
breadboards: 1

parts:
  Part1 = Arduino Uno (Rev3)
  VCC1 = Battery block 9V
  U1 = LCD-16X2 [package=lcd-16x2_noholes]
  TCS1 = TCS3200
  R1 = Rotary Potentiometer (Small) [maximum_resistance=100kΩ package=THT]
  R2 = Resistor [tolerance=±5% resistance=220 package="0603 [SMD]"]

nets:
  N1: Part1.D8, TCS1.OUT
  N2: Part1.D9_PWM, TCS1.S0
  N3: Part1.D11_PWM/MOSI, TCS1.S2
  N4: Part1.D12/MISO, TCS1.S3
  GND: Part1.GND, Part1.D5_PWM, VCC1.+, U1.VSS, U1.R_W, U1.DB7, R1.leg1
  N5: Part1.D2, U1.RS
  N6: Part1.D3_PWM, U1.E
  N7: Part1.D4, U1.DB4
  N8: Part1.D6_PWM, U1.DB5
  N9: Part1.D7, U1.DB6
  5V: Part1.5V, U1.VDD, R1.leg2, R2.Pin_1
  N10: Part1.VIN, VCC1.-
  N11: U1.VO, R1.wiper
  N12: U1.K, TCS1.GND

notes:
  Its TCS3200 color sensor....
  LCD (16 X 2)
  9V Battery
  Arduino Uno Rev 3

custom parts:
  TCS3200: COLOR SENSING TCS3200
